// Logisim project dlucs.circ as structural Verilog: 18 circuits, main circuit main
module main (
  input  Interrupt,
  input  Reset
);

  wire addrdecoder_1_br, addrdecoder_1_pr, addrdecoder_1_ram, and_1_out, clock_1_out, clockdivider_1_c0,
       clockdivider_1_c1, clockdivider_1_c2, clockdivider_1_c3, decoder_1_out0, decoder_1_out1, irq_1_out_7,
       nor24_1_out_2, or_1_out, or_2_out, s_r_ff_1_q;
  wire [2:0] and_2_out_2, multiplexer_2_out, or_3_out, State_q;
  wire [3:0] alu_1_flagout, Flags_q;
  wire [6:0] normalizer_1_q;
  wire [7:0] bootROM_data, controlled_buffer_1_out, DLatch_q, Instruction_q, mainRAM_dout, progROM_data;
  wire [15:0] A_q, ALatch_q, alu_1_d, B_q, multiplexer_1_out, multiplexer_3_out, multiplexer_4_out, PC_q,
       regbank_1_q;
  wire [15:8] DLatch_q_2, Instruction_q_2;
  wire [20:0] and_2_out;
  wire [23:0] ceu_1_r, uCode_data;

  Clock clock_1 (.out(clock_1_out));
  ClockDivider clockdivider_1 (
    .Clock(clock_1_out), .Reset(Reset), .C0(clockdivider_1_c0), .C1(clockdivider_1_c1),
    .C2(clockdivider_1_c2), .C3(clockdivider_1_c3));
  Multiplexer #(.width(16)) multiplexer_1 (.in0(PC_q), .in1(A_q), .out(multiplexer_1_out), .sel(and_2_out[20]));
  Register #(.width(16)) ALatch (.D(multiplexer_1_out), .en(1'b1), .Q(ALatch_q), .clk(clockdivider_1_c1), .clr(1'b0));
  ROM bootROM (.addr(ALatch_q[7:0]), .data(bootROM_data));
  and and_1 (and_1_out, and_2_out[4], addrdecoder_1_ram);
  RAM #(.addrWidth(15), .enables("line")) mainRAM (
    .addr(ALatch_q[14:0]), .we(and_1_out), .clk(clockdivider_1_c3), .din(DLatch_q), .dout(mainRAM_dout));
  ROM #(.addrWidth(15)) progROM (.addr(ALatch_q[14:0]), .data(progROM_data));
  Counter #(.max('hffff), .width(16)) PC (
    .load(and_2_out[5]), .D({DLatch_q_2, DLatch_q}), .count(and_2_out[19]), .Q(PC_q), .up(1'b1),
    .clk(clockdivider_1_c3), .clr(s_r_ff_1_q));  // open: carry
  S_R_Flip_Flop s_r_ff_1 (
    .S(1'b0), .clk(clock_1_out), .R(1'b1), .Q(s_r_ff_1_q), .preset(Reset), .reset(1'b0));  // open: Qn
  Counter #(.max('h7), .width(3)) State (
    .D(3'b000), .count(1'b1), .Q(State_q), .up(1'b1), .clk(clockdivider_1_c0), .clr(or_1_out));  // open: load, carry
  or or_1 (or_1_out, nor24_1_out_2, s_r_ff_1_q);
  AddrDecoder addrdecoder_1 (.A(ALatch_q), .BR(addrdecoder_1_br), .RAM(addrdecoder_1_ram), .PR(addrdecoder_1_pr));
  assign controlled_buffer_1_out = addrdecoder_1_br ? bootROM_data : 8'bz;  // Controlled_Buffer controlled_buffer_1
  assign controlled_buffer_1_out = addrdecoder_1_ram ? mainRAM_dout : 8'bz;  // Controlled_Buffer controlled_buffer_2
  assign controlled_buffer_1_out = addrdecoder_1_pr ? progROM_data : 8'bz;  // Controlled_Buffer controlled_buffer_3
  Register #(.width(16)) Instruction (
    .D({Instruction_q, controlled_buffer_1_out}), .en(or_2_out), .clk(clockdivider_1_c3),
    .Q({Instruction_q_2, Instruction_q}), .clr(s_r_ff_1_q));
  or or_2 (or_2_out, decoder_1_out1, decoder_1_out0);
  IRQ irq_1 (
    .Req(Interrupt), .State(State_q), .Clock(clockdivider_1_c0), .Reset(s_r_ff_1_q), .done(nor24_1_out_2),
    .ACK(and_2_out[15]), .out_7(irq_1_out_7));
  Decoder #(.enable("false"), .select(3)) decoder_1 (
    .out0(decoder_1_out0), .out1(decoder_1_out1), .sel(State_q));  // open: out2, out3, out4, out5, out6, out7
  CEU ceu_1 (.Flags(Flags_q), .Instr({Instruction_q_2, Instruction_q}), .Interrupt(irq_1_out_7), .R(ceu_1_r));
  Normalizer normalizer_1 (
    .State(State_q), .Instr({Instruction_q_2, Instruction_q}), .IRQ(irq_1_out_7), .Q(normalizer_1_q));
  ROM #(.addrWidth(10), .dataWidth(24)) uCode (.addr({normalizer_1_q, State_q}), .data(uCode_data));
  Multiplexer #(.width(3)) multiplexer_2 (
    .in0(Instruction_q[2:0]), .in1(Instruction_q[5:3]), .out(multiplexer_2_out), .sel(and_2_out[14]));
  assign or_3_out = {3{and_2_out[13]}} | multiplexer_2_out;  // OR_Gate or_3, 3 bits wide
  Counter #(.max('hffff), .width(16)) A (
    .load(and_2_out[3]), .D({DLatch_q_2, DLatch_q}), .count(and_2_out[18]), .Q(A_q), .up(and_2_out[17]),
    .clk(clockdivider_1_c3), .clr(1'b0));  // open: carry
  Register #(.width(16)) B (
    .D({DLatch_q_2, DLatch_q}), .en(and_2_out[2]), .clk(clockdivider_1_c3), .Q(B_q), .clr(1'b0));
  Nor24 nor24_1 (.in_1(uCode_data), .out_2(nor24_1_out_2));
  assign {and_2_out_2, and_2_out} = uCode_data & ceu_1_r;  // AND_Gate and_2, 24 bits wide
  Register #(.width(4)) Flags (.D(alu_1_flagout), .en(and_2_out[0]), .clk(clockdivider_1_c3), .Q(Flags_q), .clr(1'b0));
  Register #(.width(16)) DLatch (
    .D(multiplexer_3_out), .en(1'b1), .Q({DLatch_q_2, DLatch_q}), .clk(clockdivider_1_c2), .clr(1'b0));
  RegBank regbank_1 (
    .R(or_3_out), .D({DLatch_q_2, DLatch_q}), .WE(and_2_out[1]), .Clock(clockdivider_1_c3), .Q(regbank_1_q));
  ALU alu_1 (
    .FlagIn(Flags_q), .A(A_q), .B(B_q), .CA(and_2_out[12]), .CB(and_2_out[11]), .CD(and_2_out[10]),
    .OpSel(and_2_out[9:6]), .FlagOut(alu_1_flagout), .D(alu_1_d));
  Multiplexer #(.width(16)) multiplexer_3 (
    .in0(multiplexer_4_out), .in1({multiplexer_4_out[7:0], multiplexer_4_out[15:8]}),
    .out(multiplexer_3_out), .sel(and_2_out[16]));
  Multiplexer #(.select(3), .width(16)) multiplexer_4 (
    .in0({16{1'b0}}), .in1(16'h1), .in2(PC_q), .in3(regbank_1_q), .in4(alu_1_d),
    .in5({{8{1'b0}}, controlled_buffer_1_out}), .in6({Instruction_q_2, Instruction_q}),
    .in7({{12{1'b0}}, Flags_q}), .out(multiplexer_4_out), .sel(and_2_out_2));

  // Notes on the sheet:
  //   contents of bootROM (hex, n*v repeats v):
  //   58 7c 0 80 78 40 50 7 a0 0 48 0 a0 0 98 0 48 0 98 0 a8
  //   contents of progROM (hex, n*v repeats v):
  //   58 40 58 49 8 1 f0 1 88 75 88 f0 50 6
  //   contents of uCode (hex, n*v repeats v):
  //   682008 80000 600004 604008 804043 0 0 0 682008 80000 c00008 8003c4 604008 804043 0 0 682008 80000
  //   a80004 a90008 801804 604008 804043 0 602008 40004 550010 500010 803802 20000c 80014c 808160 682008
  //   80000 600004 604008 804083 0 0 0 682008 80000 c00008 8003c4 604008 804083 0 0 682008 80000 a80004
  //   a90008 801804 604008 804083 0 602008 40004 550010 500010 803802 20000c 80014c 808160 682008 80000
  //   600004 604008 804403 0 0 0 682008 80000 c00008 8003c4 604008 804403 0 0 682008 80000 a80004 a90008
  //   801804 604008 804403 0 602008 40004 550010 500010 803802 20000c 80014c 808160 682008 28000c 600004
  //   604008 8041c3 0 0 0 682008 28000c 8000cc 8000c4 c00008 800404 604008 8041c3 682008 28000c a80004
  //   a90008 801804 604008 8041c3 0 602008 40004 550010 500010 803802 20000c 80014c 808160 682008 c0004
  //   550010 500010 803802 600020 0 0 602008 40004 550010 500010 803802 20000c 80014c 808160 682008 c0004
  //   550010 500010 803802 a80008 a90004 801820 602008 40004 550010 500010 803802 20000c 80014c 808160
  //   682008 80000 600008 804303 4*0 682008 80000 c00008 8003c8 804303 0 0 0 682008 80000 a80004 a90008
  //   801808 804303 0 0 602008 40004 550010 500010 803802 20000c 80014c 808160 682008 80000 600008 800748
  //   804303 0 0 0 682008 80000 c00008 8003c8 800748 804303 0 0 682008 80000 a80004 a90008 801808 800748
  //   804303 0 602008 40004 550010 500010 803802 20000c 80014c 808160 682008 80000 600004 604008 8008c1 0
  //   0 0 682008 80000 c00008 8003c4 604008 8008c1 0 0 682008 80000 a80004 a90008 801804 604008 8008c1 0
  //   602008 40004 550010 500010 803802 20000c 80014c 808160 682008 80000 600008 800388 800748 804303 0 0
  //   682008 80000 c00008 8003c8 800388 800748 804303 0 682008 80000 a80004 a90008 801808 800388 800748
  //   804303 602008 40004 550010 500010 803802 20000c 80014c 808160 682008 80000 600004 e00008 800388
  //   804382 8003c1 0 602008 40004 550010 500010 803802 20000c 80014c 808160 682008 80000 a80004 e80008
  //   800388 804382 8003c1 0 602008 40004 550010 500010 803802 20000c 80014c 808160 682008 80000 600020
  //   5*0 602008 40004 550010 500010 803802 20000c 80014c 808160 682008 80000 a80008 a90004 801820 0 0 0
  //   602008 40004 550010 500010 803802 20000c 80014c 808160 682008 80000 60000c 805802 4*0 682008 80000
  //   c00008 8043c2 4*0 682008 80000 a80004 a90008 805802 0 0 0 602008 40004 550010 500010 803802 20000c
  //   80014c 808160 682008 80000 600008 b60004 b10008 805802 0 0 602008 40004 550010 500010 803802 20000c
  //   80014c 808160 682008 80000 a80004 a90008 801808 b60004 b10008 805802 602008 40004 550010 500010
  //   803802 20000c 80014c 808160 682008 28000c 600004 604008 804143 0 0 0 682008 28000c 8000cc 8000c4
  //   c00008 800404 604008 804143 682008 28000c a80004 a90008 801804 604008 804143 0 602008 40004 550010
  //   500010 803802 20000c 80014c 808160 682008 28000c 600004 604008 804183 0 0 0 682008 28000c 8000cc
  //   8000c4 c00008 800404 604008 804183 682008 28000c a80004 a90008 801804 604008 804183 0 602008 40004
  //   550010 500010 803802 20000c 80014c 808160 682008 80000 600004 8 8048c3 0 0 0 682008 80000 c00008
  //   8003c4 8 8048c3 0 0 682008 80000 a80004 a90008 801804 8 8048c3 0 602008 40004 550010 500010 803802
  //   20000c 80014c 808160 682008 80000 60000c 805c03 4*0 682008 80000 c00008 8003cc 805c03 0 0 0 682008
  //   80000 a80004 a90008 805c03 0 0 0 602008 40004 550010 500010 803802 20000c 80014c 808160 682008 80000
  //   600008 400004 804082 0 0 0 682008 80000 c00008 8003cc 800088 400004 804082 0 682008 80000 a80004
  //   a90008 801808 400004 804082 0 602008 40004 550010 500010 803802 20000c 80014c 808160 682008 80000
  //   600004 604008 805803 0 0 0 682008 80000 c00008 8003c4 604008 805803 0 0 682008 80000 a80004 a90008
  //   801804 604008 805803 0 602008 40004 550010 500010 803802 20000c 80014c 808160 682008 80000 b60004
  //   b10008 805802 602008 260004 802082 602008 40004 550010 500010 803802 20000c 80014c 808160 602008
  //   40004 550010 500010 803802 20000c 80014c 808160 602008 40004 550010 500010 803802 20000c 80014c
  //   808160 682008 c0004 750010 700010 803802 0 0 0 602008 40004 550010 500010 803802 20000c 80014c
  //   808160 602008 40004 550010 500010 803802 20000c 80014c 808160 602008 4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
endmodule

module ALU (
  input  [3:0] FlagIn,
  input  [15:0] A,
  input  [15:0] B,
  input  CA,
  input  CB,
  input  CD,
  input  [3:0] OpSel,
  output [3:0] FlagOut,
  output [15:0] D
);

  wire addsub_1_c, addsub_1_v, decoder_1_out15, rotateunit_1_c, shiftunit_1_c;
  wire [3:0] multiplexer_2_out, nor_1_out;
  wire [15:0] addsub_1_d, flooddown_1_d, multiplexer_1_out, multiplexer_4_out, nand_1_out, not_1_out,
       not_2_out, not_3_out, popc_1_c, reverse_1_d, rotateunit_1_d, shiftunit_1_d, xor_1_out;
  wire [15:4] multiplexer_2_out_2;

  Decoder #(.enable("false"), .select(4)) decoder_1 (
    .out15(decoder_1_out15), .sel(OpSel));  // open: out0, out1, out2, out3, out4, out5, out6, out7, out8, out9, out10, out11, out12, out13, out14
  Multiplexer #(.width(16)) multiplexer_1 (.in0(A), .in1(not_1_out), .out(multiplexer_1_out), .sel(CA));
  assign not_1_out = ~A;  // NOT_Gate not_1, 16 bits wide
  assign not_2_out = ~B;  // NOT_Gate not_2, 16 bits wide
  Multiplexer #(.width(16)) multiplexer_2 (
    .in0(B), .in1(not_2_out), .out({multiplexer_2_out_2, multiplexer_2_out}), .sel(CB));
  AddSub addsub_1 (
    .OpSel(OpSel), .FlagIn(FlagIn), .A(multiplexer_1_out), .B({multiplexer_2_out_2, multiplexer_2_out}),
    .D(addsub_1_d), .C(addsub_1_c), .V(addsub_1_v));
  ShiftUnit shiftunit_1 (
    .OpSel(OpSel), .A(multiplexer_1_out), .B({multiplexer_2_out_2, multiplexer_2_out}), .D(shiftunit_1_d),
    .C(shiftunit_1_c));
  RotateUnit rotateunit_1 (
    .FlagIn(FlagIn), .OpSel(OpSel), .A(multiplexer_1_out), .B({multiplexer_2_out_2, multiplexer_2_out}),
    .D(rotateunit_1_d), .C(rotateunit_1_c));
  POPC popc_1 (.A(multiplexer_1_out), .C(popc_1_c));
  FloodDown flooddown_1 (.A(multiplexer_1_out), .D(flooddown_1_d));
  Reverse reverse_1 (.A(multiplexer_1_out), .D(reverse_1_d));
  assign nand_1_out = ~(multiplexer_1_out & {multiplexer_2_out_2, multiplexer_2_out});  // NAND_Gate nand_1, 16 bits wide
  assign xor_1_out = multiplexer_1_out ^ {multiplexer_2_out_2, multiplexer_2_out};  // XOR_Gate xor_1, 16 bits wide
  Multiplexer #(.select(4)) multiplexer_3 (
    .in0(FlagIn[3]), .in1(addsub_1_c), .in2(addsub_1_c), .in3(addsub_1_c), .in4(FlagIn[3]),
    .in5(shiftunit_1_c), .in6(shiftunit_1_c), .in7(shiftunit_1_c), .in8(1'b0), .in9(rotateunit_1_c),
    .in10(1'b0), .in11(rotateunit_1_c), .in12(FlagIn[3]), .in13(FlagIn[3]), .in14(FlagIn[3]),
    .in15(FlagIn[3]), .out(nor_1_out[3]), .sel(OpSel));
  Multiplexer #(.select(4), .width(16)) multiplexer_4 (
    .in0(nand_1_out), .in1(addsub_1_d), .in2(addsub_1_d), .in3(addsub_1_d), .in4(xor_1_out),
    .in5(shiftunit_1_d), .in6(shiftunit_1_d), .in7(shiftunit_1_d), .in8(rotateunit_1_d),
    .in9(rotateunit_1_d), .in10(rotateunit_1_d), .in11(rotateunit_1_d), .in12(popc_1_c),
    .in13(flooddown_1_d), .in14(reverse_1_d), .in15({{14{multiplexer_1_out[2]}}, multiplexer_1_out[1:0]}),
    .out(multiplexer_4_out), .sel(OpSel));
  Multiplexer #(.select(4)) multiplexer_5 (
    .in0(FlagIn[1]), .in1(addsub_1_v), .in2(addsub_1_v), .in3(addsub_1_v), .in4(FlagIn[1]), .in5(1'b0),
    .in6(1'b0), .in7(1'b0), .in8(1'b0), .in9(1'b0), .in10(1'b0), .in11(1'b0), .in12(FlagIn[1]),
    .in13(FlagIn[1]), .in14(FlagIn[1]), .in15(FlagIn[1]), .out(nor_1_out[1]), .sel(OpSel));
  Multiplexer #(.width(16)) multiplexer_6 (.in0(multiplexer_4_out), .in1(not_3_out), .out(D), .sel(CD));
  assign not_3_out = ~multiplexer_4_out;  // NOT_Gate not_3, 16 bits wide
  nor nor_1 (nor_1_out[0], D[0], D[1], D[2], D[3], D[4], D[5], D[6], D[7], D[8], D[9], D[10], D[11], D[12], D[13], D[14], D[15]);
  Multiplexer #(.width(4)) multiplexer_7 (
    .in0({nor_1_out[3], D[15], nor_1_out[1:0]}), .in1(multiplexer_2_out), .out(FlagOut), .sel(decoder_1_out15));
endmodule

module AddrDecoder (
  input  [15:0] A,
  output BR,
  output RAM,
  output PR
);

  nor nor_1 (BR, A[8], A[9], A[10], A[11], A[12], A[13], A[14], A[15]);
  nor nor_2 (RAM, BR, A[15]);

  assign PR = A[15];
endmodule

module RegBank (
  input  [2:0] R,
  input  [15:0] D,
  input  WE,
  input  Clock,
  output [15:0] Q
);

  wire and_1_out, and_2_out, and_3_out, and_4_out, and_5_out, and_6_out, and_7_out, and_8_out,
       decoder_1_out0, decoder_1_out1, decoder_2_out0, decoder_2_out1, decoder_2_out2, decoder_2_out3,
       decoder_3_out0, decoder_3_out1, decoder_3_out2, decoder_3_out3;
  wire [15:0] R0_q, R1_q, R2_q, R3_q, R4_q, R5_q, R6_q, SP_q;

  Decoder #(.enable("false")) decoder_1 (.out0(decoder_1_out0), .out1(decoder_1_out1), .sel(R[2]));
  Decoder #(.select(2)) decoder_2 (
    .out0(decoder_2_out0), .out1(decoder_2_out1), .out2(decoder_2_out2), .out3(decoder_2_out3), .sel(R[1:0]),
    .en(decoder_1_out0));
  and and_1 (and_1_out, decoder_2_out0, WE);
  and and_2 (and_2_out, decoder_2_out1, WE);
  and and_3 (and_3_out, decoder_2_out2, WE);
  and and_4 (and_4_out, decoder_2_out3, WE);
  Decoder #(.select(2)) decoder_3 (
    .out0(decoder_3_out0), .out1(decoder_3_out1), .out2(decoder_3_out2), .out3(decoder_3_out3), .sel(R[1:0]),
    .en(decoder_1_out1));
  Register #(.width(16)) R0 (.D(D), .en(and_1_out), .clk(Clock), .Q(R0_q), .clr(1'b0));
  Register #(.width(16)) R1 (.D(D), .en(and_2_out), .clk(Clock), .Q(R1_q), .clr(1'b0));
  Register #(.width(16)) R2 (.D(D), .en(and_3_out), .clk(Clock), .Q(R2_q), .clr(1'b0));
  Register #(.width(16)) R3 (.D(D), .en(and_4_out), .clk(Clock), .Q(R3_q), .clr(1'b0));
  assign Q = decoder_2_out0 ? R0_q : 16'bz;  // Controlled_Buffer controlled_buffer_1
  assign Q = decoder_2_out1 ? R1_q : 16'bz;  // Controlled_Buffer controlled_buffer_2
  assign Q = decoder_2_out2 ? R2_q : 16'bz;  // Controlled_Buffer controlled_buffer_3
  assign Q = decoder_2_out3 ? R3_q : 16'bz;  // Controlled_Buffer controlled_buffer_4
  Register #(.width(16)) R4 (.D(D), .en(and_5_out), .clk(Clock), .Q(R4_q), .clr(1'b0));
  and and_5 (and_5_out, decoder_3_out0, WE);
  Register #(.width(16)) R5 (.D(D), .en(and_6_out), .clk(Clock), .Q(R5_q), .clr(1'b0));
  and and_6 (and_6_out, decoder_3_out1, WE);
  Register #(.width(16)) R6 (.D(D), .en(and_7_out), .clk(Clock), .Q(R6_q), .clr(1'b0));
  and and_7 (and_7_out, decoder_3_out2, WE);
  Register #(.width(16)) SP (.D(D), .en(and_8_out), .clk(Clock), .Q(SP_q), .clr(1'b0));
  and and_8 (and_8_out, decoder_3_out3, WE);
  assign Q = decoder_3_out0 ? R4_q : 16'bz;  // Controlled_Buffer controlled_buffer_5
  assign Q = decoder_3_out1 ? R5_q : 16'bz;  // Controlled_Buffer controlled_buffer_6
  assign Q = decoder_3_out2 ? R6_q : 16'bz;  // Controlled_Buffer controlled_buffer_7
  assign Q = decoder_3_out3 ? SP_q : 16'bz;  // Controlled_Buffer controlled_buffer_8
endmodule

module AddSub (
  input  [3:0] OpSel,
  input  [3:0] FlagIn,
  input  [15:0] A,
  input  [15:0] B,
  output [15:0] D,
  output C,
  output V
);

  wire multiplexer_1_out, xnor_1_out, xor_1_out;

  xnor xnor_1 (xnor_1_out, A[15], B[15]);
  Multiplexer multiplexer_1 (.in0(FlagIn[3]), .in1(OpSel[0]), .out(multiplexer_1_out), .sel(OpSel[1]));
  Adder #(.width(16)) adder_1 (.a(A), .b(B), .out(D), .cin(multiplexer_1_out), .cout(C));
  xor xor_1 (xor_1_out, B[15], D[15]);
  and and_1 (V, xor_1_out, xnor_1_out);

  // Notes on the sheet:
  //   CNVZ
endmodule

module Normalizer (
  input  [2:0] State,
  input  [15:0] Instr,
  input  IRQ,
  output [6:0] Q
);

  wire decoder_1_out0, decoder_1_out1, decoder_2_out3, decoder_2_out13, decoder_2_out14, decoder_2_out24,
       decoder_2_out25, decoder_2_out26, decoder_2_out27, nor_1_out, or_1_out, xnor_1_out;
  wire [1:0] and_1_out;
  wire [6:0] multiplexer_1_out, multiplexer_2_out;

  Decoder #(.enable("false"), .select(3)) decoder_1 (
    .out0(decoder_1_out0), .out1(decoder_1_out1), .sel(State));  // open: out2, out3, out4, out5, out6, out7
  // NoConnect on Instr[8]
  // NoConnect on Instr[9]
  // NoConnect on Instr[10]
  Decoder #(.enable("false"), .select(5)) decoder_2 (
    .out3(decoder_2_out3), .out13(decoder_2_out13), .out14(decoder_2_out14), .out24(decoder_2_out24),
    .out25(decoder_2_out25), .out26(decoder_2_out26), .out27(decoder_2_out27), .sel(Instr[15:11]));  // open: out0, out1, out2, out4, out5, out6, out7, out8, out9, out10, out11, out12, out15, out16, out17, out18, out19, out20, out21, out22, out23, out28, out29, out30, out31
  nor nor_1 (nor_1_out, Instr[0], Instr[1], xnor_1_out);
  or or_1 (or_1_out, decoder_2_out3, decoder_2_out13, decoder_2_out14, decoder_2_out24, decoder_2_out25, decoder_2_out26, decoder_2_out27);
  and and_1 (and_1_out[0], Instr[6], ~nor_1_out);  // AND_Gate
  and and_2 (and_1_out[1], Instr[6], nor_1_out);
  xnor xnor_1 (xnor_1_out, Instr[2], or_1_out);
  Multiplexer #(.width(7)) multiplexer_1 (
    .in0({Instr[15:11], and_1_out}), .in1({Instr[7:3], 2'b00}), .out(multiplexer_1_out), .sel(decoder_1_out1));
  Multiplexer #(.width(7)) multiplexer_2 (
    .in0(multiplexer_1_out), .in1({7{1'b0}}), .out(multiplexer_2_out), .sel(decoder_1_out0));
  assign Q = multiplexer_2_out | {{5{1'b0}}, {2{IRQ}}};  // OR_Gate or_2, 7 bits wide
endmodule

module CEU (
  input  [3:0] Flags,
  input  [15:0] Instr,
  input  Interrupt,
  output [23:0] R
);

  wire multiplexer_1_out, or_1_out, or_2_out, xor_1_out, xor_2_out;

  Multiplexer #(.select(3)) multiplexer_1 (
    .in0(1'b1), .in1(Flags[3]), .in2(Flags[2]), .in3(Flags[1]), .in4(Flags[0]), .in5(or_1_out),
    .in6(xor_2_out), .in7(or_2_out), .out(multiplexer_1_out), .sel(Instr[9:7]));
  xor xor_1 (xor_1_out, Instr[10], multiplexer_1_out);
  or or_1 (or_1_out, ~Flags[3], Flags[0]);  // OR_Gate
  xor xor_2 (xor_2_out, Flags[2], Flags[1]);
  or or_2 (or_2_out, xor_2_out, Flags[0]);
  or or_3 (R[5], xor_1_out, Interrupt);

  assign {R[23:6], R[4:0]} = {{18{1'b1}}, R[5], 2'b11, {2{R[5]}}};

  // Notes on the sheet:
  //   C
  //   N
  //   V
  //   Z
endmodule

module ShiftUnit (
  input  [3:0] OpSel,
  input  [15:0] A,
  input  [15:0] B,
  output [15:0] D,
  output C
);

  wire anyof16_1_q, anyof16_2_q, anyof16_3_q, multiplexer_2_out;
  wire [4:4] not_1_out;
  wire [15:0] multiplexer_1_out, multiplexer_3_out;
  wire [15:15] nor_1_out;
  wire [31:0] shifter_1_out, shifter_2_out, shifter_3_out;

  not not_1 (not_1_out[4], nor_1_out[15]);
  nor nor_1 (nor_1_out[15], B[4], B[5], B[6], B[7], B[8], B[9], B[10], B[11], B[12], B[13], B[14], B[15]);
  Shifter #(.width(32)) shifter_1 (.in({{16{1'b0}}, A}), .\dist ({not_1_out[4], B[3:0]}), .out(shifter_1_out));
  Shifter #(.shift("lr"), .width(32)) shifter_2 (
    .in({A, {16{1'b0}}}), .\dist ({not_1_out[4], B[3:0]}), .out(shifter_2_out));
  Shifter #(.shift("ar"), .width(32)) shifter_3 (
    .in({A, {16{1'b0}}}), .\dist ({not_1_out[4], B[3:0]}), .out(shifter_3_out));
  AnyOf16 anyof16_1 (.D(shifter_1_out[31:16]), .Q(anyof16_1_q));
  AnyOf16 anyof16_2 (.D(shifter_2_out[15:0]), .Q(anyof16_2_q));
  AnyOf16 anyof16_3 (.D(shifter_3_out[15:0]), .Q(anyof16_3_q));
  Multiplexer #(.width(16)) multiplexer_1 (
    .in0(shifter_2_out[31:16]), .in1(shifter_3_out[31:16]), .out(multiplexer_1_out), .sel(OpSel[0]));
  Multiplexer multiplexer_2 (.in0(anyof16_2_q), .in1(anyof16_3_q), .out(multiplexer_2_out), .sel(OpSel[0]));
  Multiplexer #(.width(16)) multiplexer_3 (
    .in0(shifter_1_out[15:0]), .in1(multiplexer_1_out), .out(multiplexer_3_out), .sel(OpSel[1]));
  Multiplexer multiplexer_4 (.in0(anyof16_1_q), .in1(multiplexer_2_out), .out(C), .sel(OpSel[1]));
  assign D = multiplexer_3_out & {16{nor_1_out[15]}};  // AND_Gate and_1, 16 bits wide
endmodule

module AnyOf16 (
  input  [15:0] D,
  output Q
);

  or or_1 (Q, D[0], D[1], D[2], D[3], D[4], D[5], D[6], D[7], D[8], D[9], D[10], D[11], D[12], D[13], D[14], D[15]);
endmodule

module RotateUnit (
  input  [3:0] FlagIn,
  input  [3:0] OpSel,
  input  [15:0] A,
  input  [15:0] B,
  output [15:0] D,
  output C
);

  wire multiplexer_4_out;
  wire [4:0] mod17_1_q;
  wire [15:0] multiplexer_1_out, multiplexer_2_out, shifter_1_out, shifter_3_out;
  wire [16:0] shifter_2_out, shifter_4_out;

  Mod17 mod17_1 (.D(B), .Q(mod17_1_q));
  Shifter #(.shift("rl"), .width(16)) shifter_1 (.in(A), .\dist (B[3:0]), .out(shifter_1_out));
  Shifter #(.shift("rl"), .width(17)) shifter_2 (.in({FlagIn[3], A}), .\dist (mod17_1_q), .out(shifter_2_out));
  Shifter #(.shift("rr"), .width(16)) shifter_3 (.in(A), .\dist (B[3:0]), .out(shifter_3_out));
  Shifter #(.shift("rr"), .width(17)) shifter_4 (.in({FlagIn[3], A}), .\dist (mod17_1_q), .out(shifter_4_out));
  Multiplexer #(.width(16)) multiplexer_1 (
    .in0(shifter_1_out), .in1(shifter_2_out[15:0]), .out(multiplexer_1_out), .sel(OpSel[0]));
  Multiplexer #(.width(16)) multiplexer_2 (
    .in0(shifter_3_out), .in1(shifter_4_out[15:0]), .out(multiplexer_2_out), .sel(OpSel[0]));
  Multiplexer #(.width(16)) multiplexer_3 (.in0(multiplexer_1_out), .in1(multiplexer_2_out), .out(D), .sel(OpSel[1]));
  Multiplexer multiplexer_4 (.in0(shifter_2_out[16]), .in1(shifter_4_out[16]), .out(multiplexer_4_out), .sel(OpSel[1]));
  and and_1 (C, OpSel[0], multiplexer_4_out);
endmodule

module POPC (
  input  [15:0] A,
  output [15:0] C
);

  wire adder_1_cout, adder_1_out, adder_8_cout, adder_8_out, or_1_out;
  wire [1:0] adder_2_out, adder_3_out, adder_4_out, adder_5_out, adder_6_out, adder_7_out;
  wire [2:2] adder_6_cout, adder_7_cout;
  wire [3:0] adder_9_out;
  wire [4:4] adder_9_cout;

  Adder #(.width(1)) adder_1 (.a(A[1]), .b(A[2]), .out(adder_1_out), .cin(A[0]), .cout(adder_1_cout));
  Adder #(.width(1)) adder_2 (.a(A[4]), .b(A[5]), .out(adder_2_out[0]), .cin(A[3]), .cout(adder_2_out[1]));
  Adder #(.width(1)) adder_3 (.a(A[7]), .b(A[8]), .out(adder_3_out[0]), .cin(A[6]), .cout(adder_3_out[1]));
  Adder #(.width(1)) adder_4 (.a(A[10]), .b(A[11]), .out(adder_4_out[0]), .cin(A[9]), .cout(adder_4_out[1]));
  Adder #(.width(1)) adder_5 (.a(A[13]), .b(A[14]), .out(adder_5_out[0]), .cin(A[12]), .cout(adder_5_out[1]));
  Adder #(.width(2)) adder_6 (
    .a(adder_2_out), .b(adder_3_out), .out(adder_6_out), .cin(adder_1_out), .cout(adder_6_cout[2]));
  Adder #(.width(2)) adder_7 (
    .a(adder_4_out), .b(adder_5_out), .out(adder_7_out), .cin(adder_1_cout), .cout(adder_7_cout[2]));
  Adder #(.width(1)) adder_8 (.a(adder_1_cout), .b(A[15]), .out(adder_8_out), .cin(1'b0), .cout(adder_8_cout));
  Adder #(.width(4)) adder_9 (
    .a({1'b0, adder_6_cout[2], adder_6_out}), .b({1'b0, adder_7_cout[2], adder_7_out}), .out(adder_9_out),
    .cin(adder_8_cout), .cout(adder_9_cout[4]));
  or or_1 (or_1_out, adder_8_out, adder_8_cout);
  Adder #(.width(5)) adder_10 (
    .a({5{1'b0}}), .b({adder_9_cout[4], adder_9_out}), .out(C[4:0]), .cin(or_1_out));  // open: cout

  assign C[15:5] = {11{1'b0}};
endmodule

module FloodDown (
  input  [15:0] A,
  output [15:0] D
);

  or or_1 (D[14], A[14], A[15]);
  or or_2 (D[12], A[12], D[13]);
  or or_3 (D[13], A[13], D[14]);
  or or_4 (D[11], A[11], D[12]);
  or or_5 (D[9], A[9], D[10]);
  or or_6 (D[10], A[10], D[11]);
  or or_7 (D[8], A[8], D[9]);
  or or_8 (D[6], A[6], D[7]);
  or or_9 (D[7], A[7], D[8]);
  or or_10 (D[4], A[4], D[5]);
  or or_11 (D[5], A[5], D[6]);
  or or_12 (D[3], A[3], D[4]);
  or or_13 (D[1], A[1], D[2]);
  or or_14 (D[2], A[2], D[3]);
  or or_15 (D[0], A[0], D[1]);

  assign D[15] = A[15];
endmodule

module Reverse (
  input  [15:0] A,
  output [15:0] D
);


  assign D = {A[0], A[1], A[2], A[3], A[4], A[5], A[6], A[7], A[8], A[9], A[10], A[11], A[12], A[13], A[14], A[15]};
endmodule

module Mod17Step (
  input  B,
  input  D0,
  input  D1,
  input  D2,
  input  D3,
  input  D4,
  input  D5,
  input  D6,
  input  D7,
  input  D8,
  input  D9,
  input  D10,
  input  D11,
  input  D12,
  input  D13,
  input  D14,
  input  D15,
  input  D16,
  output P,
  output Q0,
  output Q1,
  output Q2,
  output Q3,
  output Q4,
  output Q5,
  output Q6,
  output Q7,
  output Q8,
  output Q9,
  output Q10,
  output Q11,
  output Q12,
  output Q13,
  output Q14,
  output Q15,
  output Q16
);

  Multiplexer #(.width(17)) multiplexer_1 (
    .in0({D8, D16, D7, D15, D6, D14, D5, D13, D4, D12, D3, D11, D2, D10, D1, D9, D0}),
    .in1({D16, D7, D15, D6, D14, D5, D13, D4, D12, D3, D11, D2, D10, D1, D9, D0, D8}),
    .out({Q16, Q15, Q14, Q13, Q12, Q11, Q10, Q9, Q8, Q7, Q6, Q5, Q4, Q3, Q2, Q1, Q0}), .sel(B));

  assign P = B;
endmodule

module Mod17 (
  input  [15:0] D,
  output [4:0] Q
);

  wire mod17step_1_q0, mod17step_1_q1, mod17step_1_q2, mod17step_1_q3, mod17step_1_q4, mod17step_1_q5,
       mod17step_1_q6, mod17step_1_q7, mod17step_1_q8, mod17step_1_q9, mod17step_1_q10, mod17step_1_q11,
       mod17step_1_q12, mod17step_1_q13, mod17step_1_q14, mod17step_1_q15, mod17step_1_q16, mod17step_2_q0,
       mod17step_2_q1, mod17step_2_q2, mod17step_2_q3, mod17step_2_q4, mod17step_2_q5, mod17step_2_q6,
       mod17step_2_q7, mod17step_2_q8, mod17step_2_q9, mod17step_2_q10, mod17step_2_q11, mod17step_2_q12,
       mod17step_2_q13, mod17step_2_q14, mod17step_2_q15, mod17step_2_q16, mod17step_3_q0, mod17step_3_q1,
       mod17step_3_q2, mod17step_3_q3, mod17step_3_q4, mod17step_3_q5, mod17step_3_q6, mod17step_3_q7,
       mod17step_3_q8, mod17step_3_q9, mod17step_3_q10, mod17step_3_q11, mod17step_3_q12, mod17step_3_q13,
       mod17step_3_q14, mod17step_3_q15, mod17step_3_q16, mod17step_4_q0, mod17step_4_q1, mod17step_4_q2,
       mod17step_4_q3, mod17step_4_q4, mod17step_4_q5, mod17step_4_q6, mod17step_4_q7, mod17step_4_q8,
       mod17step_4_q9, mod17step_4_q10, mod17step_4_q11, mod17step_4_q12, mod17step_4_q13, mod17step_4_q14,
       mod17step_4_q15, mod17step_4_q16, mod17step_5_q0, mod17step_5_q1, mod17step_5_q2, mod17step_5_q3,
       mod17step_5_q4, mod17step_5_q5, mod17step_5_q6, mod17step_5_q7, mod17step_5_q8, mod17step_5_q9,
       mod17step_5_q10, mod17step_5_q11, mod17step_5_q12, mod17step_5_q13, mod17step_5_q14, mod17step_5_q15,
       mod17step_5_q16, mod17step_6_q0, mod17step_6_q1, mod17step_6_q2, mod17step_6_q3, mod17step_6_q4,
       mod17step_6_q5, mod17step_6_q6, mod17step_6_q7, mod17step_6_q8, mod17step_6_q9, mod17step_6_q10,
       mod17step_6_q11, mod17step_6_q12, mod17step_6_q13, mod17step_6_q14, mod17step_6_q15, mod17step_6_q16,
       mod17step_7_q0, mod17step_7_q1, mod17step_7_q2, mod17step_7_q3, mod17step_7_q4, mod17step_7_q5,
       mod17step_7_q6, mod17step_7_q7, mod17step_7_q8, mod17step_7_q9, mod17step_7_q10, mod17step_7_q11,
       mod17step_7_q12, mod17step_7_q13, mod17step_7_q14, mod17step_7_q15, mod17step_7_q16, mod17step_8_q0,
       mod17step_8_q1, mod17step_8_q2, mod17step_8_q3, mod17step_8_q4, mod17step_8_q5, mod17step_8_q6,
       mod17step_8_q7, mod17step_8_q8, mod17step_8_q9, mod17step_8_q10, mod17step_8_q11, mod17step_8_q12,
       mod17step_8_q13, mod17step_8_q14, mod17step_8_q15, mod17step_8_q16, mod17step_9_q0, mod17step_9_q1,
       mod17step_9_q2, mod17step_9_q3, mod17step_9_q4, mod17step_9_q5, mod17step_9_q6, mod17step_9_q7,
       mod17step_9_q8, mod17step_9_q9, mod17step_9_q10, mod17step_9_q11, mod17step_9_q12, mod17step_9_q13,
       mod17step_9_q14, mod17step_9_q15, mod17step_9_q16, mod17step_10_q0, mod17step_10_q1, mod17step_10_q2,
       mod17step_10_q3, mod17step_10_q4, mod17step_10_q5, mod17step_10_q6, mod17step_10_q7, mod17step_10_q8,
       mod17step_10_q9, mod17step_10_q10, mod17step_10_q11, mod17step_10_q12, mod17step_10_q13,
       mod17step_10_q14, mod17step_10_q15, mod17step_10_q16, mod17step_11_q0, mod17step_11_q1,
       mod17step_11_q2, mod17step_11_q3, mod17step_11_q4, mod17step_11_q5, mod17step_11_q6, mod17step_11_q7,
       mod17step_11_q8, mod17step_11_q9, mod17step_11_q10, mod17step_11_q11, mod17step_11_q12,
       mod17step_11_q13, mod17step_11_q14, mod17step_11_q15, mod17step_11_q16, mod17step_12_q0,
       mod17step_12_q1, mod17step_12_q2, mod17step_12_q3, mod17step_12_q4, mod17step_12_q5, mod17step_12_q6,
       mod17step_12_q7, mod17step_12_q8, mod17step_12_q9, mod17step_12_q10, mod17step_12_q11,
       mod17step_12_q12, mod17step_12_q13, mod17step_12_q14, mod17step_12_q15, mod17step_12_q16,
       mod17step_13_q0, mod17step_13_q1, mod17step_13_q2, mod17step_13_q3, mod17step_13_q4, mod17step_13_q5,
       mod17step_13_q6, mod17step_13_q7, mod17step_13_q8, mod17step_13_q9, mod17step_13_q10,
       mod17step_13_q11, mod17step_13_q12, mod17step_13_q13, mod17step_13_q14, mod17step_13_q15,
       mod17step_13_q16, mod17step_14_q0, mod17step_14_q1, mod17step_14_q2, mod17step_14_q3, mod17step_14_q4,
       mod17step_14_q5, mod17step_14_q6, mod17step_14_q7, mod17step_14_q8, mod17step_14_q9, mod17step_14_q10,
       mod17step_14_q11, mod17step_14_q12, mod17step_14_q13, mod17step_14_q14, mod17step_14_q15,
       mod17step_14_q16, mod17step_15_q0, mod17step_15_q1, mod17step_15_q2, mod17step_15_q3, mod17step_15_q4,
       mod17step_15_q5, mod17step_15_q6, mod17step_15_q7, mod17step_15_q8, mod17step_15_q9, mod17step_15_q10,
       mod17step_15_q11, mod17step_15_q12, mod17step_15_q13, mod17step_15_q14, mod17step_15_q15,
       mod17step_15_q16, mod17step_16_q0, mod17step_16_q1, mod17step_16_q2, mod17step_16_q3, mod17step_16_q4,
       mod17step_16_q5, mod17step_16_q6, mod17step_16_q7, mod17step_16_q8, mod17step_16_q9, mod17step_16_q10,
       mod17step_16_q11, mod17step_16_q12, mod17step_16_q13, mod17step_16_q14, mod17step_16_q15,
       mod17step_16_q16;

  Mod17Step mod17step_1 (
    .B(D[15]), .D0(1'b1), .D1(1'b0), .D2(1'b0), .D3(1'b0), .D4(1'b0), .D5(1'b0), .D6(1'b0), .D7(1'b0),
    .D8(1'b0), .D9(1'b0), .D10(1'b0), .D11(1'b0), .D12(1'b0), .D13(1'b0), .D14(1'b0), .D15(1'b0), .D16(1'b0),
    .Q0(mod17step_1_q0), .Q1(mod17step_1_q1), .Q2(mod17step_1_q2), .Q3(mod17step_1_q3), .Q4(mod17step_1_q4),
    .Q5(mod17step_1_q5), .Q6(mod17step_1_q6), .Q7(mod17step_1_q7), .Q8(mod17step_1_q8), .Q9(mod17step_1_q9),
    .Q10(mod17step_1_q10), .Q11(mod17step_1_q11), .Q12(mod17step_1_q12), .Q13(mod17step_1_q13),
    .Q14(mod17step_1_q14), .Q15(mod17step_1_q15), .Q16(mod17step_1_q16));  // open: P
  Mod17Step mod17step_2 (
    .B(D[14]), .D0(mod17step_1_q0), .D1(mod17step_1_q1), .D2(mod17step_1_q2), .D3(mod17step_1_q3),
    .D4(mod17step_1_q4), .D5(mod17step_1_q5), .D6(mod17step_1_q6), .D7(mod17step_1_q7), .D8(mod17step_1_q8),
    .D9(mod17step_1_q9), .D10(mod17step_1_q10), .D11(mod17step_1_q11), .D12(mod17step_1_q12),
    .D13(mod17step_1_q13), .D14(mod17step_1_q14), .D15(mod17step_1_q15), .D16(mod17step_1_q16),
    .Q0(mod17step_2_q0), .Q1(mod17step_2_q1), .Q2(mod17step_2_q2), .Q3(mod17step_2_q3), .Q4(mod17step_2_q4),
    .Q5(mod17step_2_q5), .Q6(mod17step_2_q6), .Q7(mod17step_2_q7), .Q8(mod17step_2_q8), .Q9(mod17step_2_q9),
    .Q10(mod17step_2_q10), .Q11(mod17step_2_q11), .Q12(mod17step_2_q12), .Q13(mod17step_2_q13),
    .Q14(mod17step_2_q14), .Q15(mod17step_2_q15), .Q16(mod17step_2_q16));  // open: P
  Mod17Step mod17step_3 (
    .B(D[13]), .D0(mod17step_2_q0), .D1(mod17step_2_q1), .D2(mod17step_2_q2), .D3(mod17step_2_q3),
    .D4(mod17step_2_q4), .D5(mod17step_2_q5), .D6(mod17step_2_q6), .D7(mod17step_2_q7), .D8(mod17step_2_q8),
    .D9(mod17step_2_q9), .D10(mod17step_2_q10), .D11(mod17step_2_q11), .D12(mod17step_2_q12),
    .D13(mod17step_2_q13), .D14(mod17step_2_q14), .D15(mod17step_2_q15), .D16(mod17step_2_q16),
    .Q0(mod17step_3_q0), .Q1(mod17step_3_q1), .Q2(mod17step_3_q2), .Q3(mod17step_3_q3), .Q4(mod17step_3_q4),
    .Q5(mod17step_3_q5), .Q6(mod17step_3_q6), .Q7(mod17step_3_q7), .Q8(mod17step_3_q8), .Q9(mod17step_3_q9),
    .Q10(mod17step_3_q10), .Q11(mod17step_3_q11), .Q12(mod17step_3_q12), .Q13(mod17step_3_q13),
    .Q14(mod17step_3_q14), .Q15(mod17step_3_q15), .Q16(mod17step_3_q16));  // open: P
  Mod17Step mod17step_4 (
    .B(D[12]), .D0(mod17step_3_q0), .D1(mod17step_3_q1), .D2(mod17step_3_q2), .D3(mod17step_3_q3),
    .D4(mod17step_3_q4), .D5(mod17step_3_q5), .D6(mod17step_3_q6), .D7(mod17step_3_q7), .D8(mod17step_3_q8),
    .D9(mod17step_3_q9), .D10(mod17step_3_q10), .D11(mod17step_3_q11), .D12(mod17step_3_q12),
    .D13(mod17step_3_q13), .D14(mod17step_3_q14), .D15(mod17step_3_q15), .D16(mod17step_3_q16),
    .Q0(mod17step_4_q0), .Q1(mod17step_4_q1), .Q2(mod17step_4_q2), .Q3(mod17step_4_q3), .Q4(mod17step_4_q4),
    .Q5(mod17step_4_q5), .Q6(mod17step_4_q6), .Q7(mod17step_4_q7), .Q8(mod17step_4_q8), .Q9(mod17step_4_q9),
    .Q10(mod17step_4_q10), .Q11(mod17step_4_q11), .Q12(mod17step_4_q12), .Q13(mod17step_4_q13),
    .Q14(mod17step_4_q14), .Q15(mod17step_4_q15), .Q16(mod17step_4_q16));  // open: P
  Mod17Step mod17step_5 (
    .B(D[11]), .D0(mod17step_4_q0), .D1(mod17step_4_q1), .D2(mod17step_4_q2), .D3(mod17step_4_q3),
    .D4(mod17step_4_q4), .D5(mod17step_4_q5), .D6(mod17step_4_q6), .D7(mod17step_4_q7), .D8(mod17step_4_q8),
    .D9(mod17step_4_q9), .D10(mod17step_4_q10), .D11(mod17step_4_q11), .D12(mod17step_4_q12),
    .D13(mod17step_4_q13), .D14(mod17step_4_q14), .D15(mod17step_4_q15), .D16(mod17step_4_q16),
    .Q0(mod17step_5_q0), .Q1(mod17step_5_q1), .Q2(mod17step_5_q2), .Q3(mod17step_5_q3), .Q4(mod17step_5_q4),
    .Q5(mod17step_5_q5), .Q6(mod17step_5_q6), .Q7(mod17step_5_q7), .Q8(mod17step_5_q8), .Q9(mod17step_5_q9),
    .Q10(mod17step_5_q10), .Q11(mod17step_5_q11), .Q12(mod17step_5_q12), .Q13(mod17step_5_q13),
    .Q14(mod17step_5_q14), .Q15(mod17step_5_q15), .Q16(mod17step_5_q16));  // open: P
  Mod17Step mod17step_6 (
    .B(D[10]), .D0(mod17step_5_q0), .D1(mod17step_5_q1), .D2(mod17step_5_q2), .D3(mod17step_5_q3),
    .D4(mod17step_5_q4), .D5(mod17step_5_q5), .D6(mod17step_5_q6), .D7(mod17step_5_q7), .D8(mod17step_5_q8),
    .D9(mod17step_5_q9), .D10(mod17step_5_q10), .D11(mod17step_5_q11), .D12(mod17step_5_q12),
    .D13(mod17step_5_q13), .D14(mod17step_5_q14), .D15(mod17step_5_q15), .D16(mod17step_5_q16),
    .Q0(mod17step_6_q0), .Q1(mod17step_6_q1), .Q2(mod17step_6_q2), .Q3(mod17step_6_q3), .Q4(mod17step_6_q4),
    .Q5(mod17step_6_q5), .Q6(mod17step_6_q6), .Q7(mod17step_6_q7), .Q8(mod17step_6_q8), .Q9(mod17step_6_q9),
    .Q10(mod17step_6_q10), .Q11(mod17step_6_q11), .Q12(mod17step_6_q12), .Q13(mod17step_6_q13),
    .Q14(mod17step_6_q14), .Q15(mod17step_6_q15), .Q16(mod17step_6_q16));  // open: P
  Mod17Step mod17step_7 (
    .B(D[9]), .D0(mod17step_6_q0), .D1(mod17step_6_q1), .D2(mod17step_6_q2), .D3(mod17step_6_q3),
    .D4(mod17step_6_q4), .D5(mod17step_6_q5), .D6(mod17step_6_q6), .D7(mod17step_6_q7), .D8(mod17step_6_q8),
    .D9(mod17step_6_q9), .D10(mod17step_6_q10), .D11(mod17step_6_q11), .D12(mod17step_6_q12),
    .D13(mod17step_6_q13), .D14(mod17step_6_q14), .D15(mod17step_6_q15), .D16(mod17step_6_q16),
    .Q0(mod17step_7_q0), .Q1(mod17step_7_q1), .Q2(mod17step_7_q2), .Q3(mod17step_7_q3), .Q4(mod17step_7_q4),
    .Q5(mod17step_7_q5), .Q6(mod17step_7_q6), .Q7(mod17step_7_q7), .Q8(mod17step_7_q8), .Q9(mod17step_7_q9),
    .Q10(mod17step_7_q10), .Q11(mod17step_7_q11), .Q12(mod17step_7_q12), .Q13(mod17step_7_q13),
    .Q14(mod17step_7_q14), .Q15(mod17step_7_q15), .Q16(mod17step_7_q16));  // open: P
  Mod17Step mod17step_8 (
    .B(D[8]), .D0(mod17step_7_q0), .D1(mod17step_7_q1), .D2(mod17step_7_q2), .D3(mod17step_7_q3),
    .D4(mod17step_7_q4), .D5(mod17step_7_q5), .D6(mod17step_7_q6), .D7(mod17step_7_q7), .D8(mod17step_7_q8),
    .D9(mod17step_7_q9), .D10(mod17step_7_q10), .D11(mod17step_7_q11), .D12(mod17step_7_q12),
    .D13(mod17step_7_q13), .D14(mod17step_7_q14), .D15(mod17step_7_q15), .D16(mod17step_7_q16),
    .Q0(mod17step_8_q0), .Q1(mod17step_8_q1), .Q2(mod17step_8_q2), .Q3(mod17step_8_q3), .Q4(mod17step_8_q4),
    .Q5(mod17step_8_q5), .Q6(mod17step_8_q6), .Q7(mod17step_8_q7), .Q8(mod17step_8_q8), .Q9(mod17step_8_q9),
    .Q10(mod17step_8_q10), .Q11(mod17step_8_q11), .Q12(mod17step_8_q12), .Q13(mod17step_8_q13),
    .Q14(mod17step_8_q14), .Q15(mod17step_8_q15), .Q16(mod17step_8_q16));  // open: P
  Mod17Step mod17step_9 (
    .B(D[7]), .D0(mod17step_8_q0), .D1(mod17step_8_q1), .D2(mod17step_8_q2), .D3(mod17step_8_q3),
    .D4(mod17step_8_q4), .D5(mod17step_8_q5), .D6(mod17step_8_q6), .D7(mod17step_8_q7), .D8(mod17step_8_q8),
    .D9(mod17step_8_q9), .D10(mod17step_8_q10), .D11(mod17step_8_q11), .D12(mod17step_8_q12),
    .D13(mod17step_8_q13), .D14(mod17step_8_q14), .D15(mod17step_8_q15), .D16(mod17step_8_q16),
    .Q0(mod17step_9_q0), .Q1(mod17step_9_q1), .Q2(mod17step_9_q2), .Q3(mod17step_9_q3), .Q4(mod17step_9_q4),
    .Q5(mod17step_9_q5), .Q6(mod17step_9_q6), .Q7(mod17step_9_q7), .Q8(mod17step_9_q8), .Q9(mod17step_9_q9),
    .Q10(mod17step_9_q10), .Q11(mod17step_9_q11), .Q12(mod17step_9_q12), .Q13(mod17step_9_q13),
    .Q14(mod17step_9_q14), .Q15(mod17step_9_q15), .Q16(mod17step_9_q16));  // open: P
  Mod17Step mod17step_10 (
    .B(D[6]), .D0(mod17step_9_q0), .D1(mod17step_9_q1), .D2(mod17step_9_q2), .D3(mod17step_9_q3),
    .D4(mod17step_9_q4), .D5(mod17step_9_q5), .D6(mod17step_9_q6), .D7(mod17step_9_q7), .D8(mod17step_9_q8),
    .D9(mod17step_9_q9), .D10(mod17step_9_q10), .D11(mod17step_9_q11), .D12(mod17step_9_q12),
    .D13(mod17step_9_q13), .D14(mod17step_9_q14), .D15(mod17step_9_q15), .D16(mod17step_9_q16),
    .Q0(mod17step_10_q0), .Q1(mod17step_10_q1), .Q2(mod17step_10_q2), .Q3(mod17step_10_q3),
    .Q4(mod17step_10_q4), .Q5(mod17step_10_q5), .Q6(mod17step_10_q6), .Q7(mod17step_10_q7),
    .Q8(mod17step_10_q8), .Q9(mod17step_10_q9), .Q10(mod17step_10_q10), .Q11(mod17step_10_q11),
    .Q12(mod17step_10_q12), .Q13(mod17step_10_q13), .Q14(mod17step_10_q14), .Q15(mod17step_10_q15),
    .Q16(mod17step_10_q16));  // open: P
  Mod17Step mod17step_11 (
    .B(D[5]), .D0(mod17step_10_q0), .D1(mod17step_10_q1), .D2(mod17step_10_q2), .D3(mod17step_10_q3),
    .D4(mod17step_10_q4), .D5(mod17step_10_q5), .D6(mod17step_10_q6), .D7(mod17step_10_q7),
    .D8(mod17step_10_q8), .D9(mod17step_10_q9), .D10(mod17step_10_q10), .D11(mod17step_10_q11),
    .D12(mod17step_10_q12), .D13(mod17step_10_q13), .D14(mod17step_10_q14), .D15(mod17step_10_q15),
    .D16(mod17step_10_q16), .Q0(mod17step_11_q0), .Q1(mod17step_11_q1), .Q2(mod17step_11_q2),
    .Q3(mod17step_11_q3), .Q4(mod17step_11_q4), .Q5(mod17step_11_q5), .Q6(mod17step_11_q6),
    .Q7(mod17step_11_q7), .Q8(mod17step_11_q8), .Q9(mod17step_11_q9), .Q10(mod17step_11_q10),
    .Q11(mod17step_11_q11), .Q12(mod17step_11_q12), .Q13(mod17step_11_q13), .Q14(mod17step_11_q14),
    .Q15(mod17step_11_q15), .Q16(mod17step_11_q16));  // open: P
  Mod17Step mod17step_12 (
    .B(D[4]), .D0(mod17step_11_q0), .D1(mod17step_11_q1), .D2(mod17step_11_q2), .D3(mod17step_11_q3),
    .D4(mod17step_11_q4), .D5(mod17step_11_q5), .D6(mod17step_11_q6), .D7(mod17step_11_q7),
    .D8(mod17step_11_q8), .D9(mod17step_11_q9), .D10(mod17step_11_q10), .D11(mod17step_11_q11),
    .D12(mod17step_11_q12), .D13(mod17step_11_q13), .D14(mod17step_11_q14), .D15(mod17step_11_q15),
    .D16(mod17step_11_q16), .Q0(mod17step_12_q0), .Q1(mod17step_12_q1), .Q2(mod17step_12_q2),
    .Q3(mod17step_12_q3), .Q4(mod17step_12_q4), .Q5(mod17step_12_q5), .Q6(mod17step_12_q6),
    .Q7(mod17step_12_q7), .Q8(mod17step_12_q8), .Q9(mod17step_12_q9), .Q10(mod17step_12_q10),
    .Q11(mod17step_12_q11), .Q12(mod17step_12_q12), .Q13(mod17step_12_q13), .Q14(mod17step_12_q14),
    .Q15(mod17step_12_q15), .Q16(mod17step_12_q16));  // open: P
  Mod17Step mod17step_13 (
    .B(D[3]), .D0(mod17step_12_q0), .D1(mod17step_12_q1), .D2(mod17step_12_q2), .D3(mod17step_12_q3),
    .D4(mod17step_12_q4), .D5(mod17step_12_q5), .D6(mod17step_12_q6), .D7(mod17step_12_q7),
    .D8(mod17step_12_q8), .D9(mod17step_12_q9), .D10(mod17step_12_q10), .D11(mod17step_12_q11),
    .D12(mod17step_12_q12), .D13(mod17step_12_q13), .D14(mod17step_12_q14), .D15(mod17step_12_q15),
    .D16(mod17step_12_q16), .Q0(mod17step_13_q0), .Q1(mod17step_13_q1), .Q2(mod17step_13_q2),
    .Q3(mod17step_13_q3), .Q4(mod17step_13_q4), .Q5(mod17step_13_q5), .Q6(mod17step_13_q6),
    .Q7(mod17step_13_q7), .Q8(mod17step_13_q8), .Q9(mod17step_13_q9), .Q10(mod17step_13_q10),
    .Q11(mod17step_13_q11), .Q12(mod17step_13_q12), .Q13(mod17step_13_q13), .Q14(mod17step_13_q14),
    .Q15(mod17step_13_q15), .Q16(mod17step_13_q16));  // open: P
  Mod17Step mod17step_14 (
    .B(D[2]), .D0(mod17step_13_q0), .D1(mod17step_13_q1), .D2(mod17step_13_q2), .D3(mod17step_13_q3),
    .D4(mod17step_13_q4), .D5(mod17step_13_q5), .D6(mod17step_13_q6), .D7(mod17step_13_q7),
    .D8(mod17step_13_q8), .D9(mod17step_13_q9), .D10(mod17step_13_q10), .D11(mod17step_13_q11),
    .D12(mod17step_13_q12), .D13(mod17step_13_q13), .D14(mod17step_13_q14), .D15(mod17step_13_q15),
    .D16(mod17step_13_q16), .Q0(mod17step_14_q0), .Q1(mod17step_14_q1), .Q2(mod17step_14_q2),
    .Q3(mod17step_14_q3), .Q4(mod17step_14_q4), .Q5(mod17step_14_q5), .Q6(mod17step_14_q6),
    .Q7(mod17step_14_q7), .Q8(mod17step_14_q8), .Q9(mod17step_14_q9), .Q10(mod17step_14_q10),
    .Q11(mod17step_14_q11), .Q12(mod17step_14_q12), .Q13(mod17step_14_q13), .Q14(mod17step_14_q14),
    .Q15(mod17step_14_q15), .Q16(mod17step_14_q16));  // open: P
  Mod17Step mod17step_15 (
    .B(D[1]), .D0(mod17step_14_q0), .D1(mod17step_14_q1), .D2(mod17step_14_q2), .D3(mod17step_14_q3),
    .D4(mod17step_14_q4), .D5(mod17step_14_q5), .D6(mod17step_14_q6), .D7(mod17step_14_q7),
    .D8(mod17step_14_q8), .D9(mod17step_14_q9), .D10(mod17step_14_q10), .D11(mod17step_14_q11),
    .D12(mod17step_14_q12), .D13(mod17step_14_q13), .D14(mod17step_14_q14), .D15(mod17step_14_q15),
    .D16(mod17step_14_q16), .Q0(mod17step_15_q0), .Q1(mod17step_15_q1), .Q2(mod17step_15_q2),
    .Q3(mod17step_15_q3), .Q4(mod17step_15_q4), .Q5(mod17step_15_q5), .Q6(mod17step_15_q6),
    .Q7(mod17step_15_q7), .Q8(mod17step_15_q8), .Q9(mod17step_15_q9), .Q10(mod17step_15_q10),
    .Q11(mod17step_15_q11), .Q12(mod17step_15_q12), .Q13(mod17step_15_q13), .Q14(mod17step_15_q14),
    .Q15(mod17step_15_q15), .Q16(mod17step_15_q16));  // open: P
  Mod17Step mod17step_16 (
    .B(D[0]), .D0(mod17step_15_q0), .D1(mod17step_15_q1), .D2(mod17step_15_q2), .D3(mod17step_15_q3),
    .D4(mod17step_15_q4), .D5(mod17step_15_q5), .D6(mod17step_15_q6), .D7(mod17step_15_q7),
    .D8(mod17step_15_q8), .D9(mod17step_15_q9), .D10(mod17step_15_q10), .D11(mod17step_15_q11),
    .D12(mod17step_15_q12), .D13(mod17step_15_q13), .D14(mod17step_15_q14), .D15(mod17step_15_q15),
    .D16(mod17step_15_q16), .Q0(mod17step_16_q0), .Q1(mod17step_16_q1), .Q2(mod17step_16_q2),
    .Q3(mod17step_16_q3), .Q4(mod17step_16_q4), .Q5(mod17step_16_q5), .Q6(mod17step_16_q6),
    .Q7(mod17step_16_q7), .Q8(mod17step_16_q8), .Q9(mod17step_16_q9), .Q10(mod17step_16_q10),
    .Q11(mod17step_16_q11), .Q12(mod17step_16_q12), .Q13(mod17step_16_q13), .Q14(mod17step_16_q14),
    .Q15(mod17step_16_q15), .Q16(mod17step_16_q16));  // open: P
  Priority_Encoder #(.select(5)) priority_encoder_1 (
    .in0(mod17step_16_q0), .in1(mod17step_16_q1), .in2(mod17step_16_q2), .in3(mod17step_16_q3),
    .in4(mod17step_16_q4), .in5(mod17step_16_q5), .in6(mod17step_16_q6), .in7(mod17step_16_q7),
    .in8(mod17step_16_q8), .in9(mod17step_16_q9), .in10(mod17step_16_q10), .in11(mod17step_16_q11),
    .in12(mod17step_16_q12), .in13(mod17step_16_q13), .in14(mod17step_16_q14), .in15(mod17step_16_q15),
    .in16(mod17step_16_q16), .in17(1'b0), .in18(1'b0), .in19(1'b0), .in20(1'b0), .in21(1'b0), .in22(1'b0),
    .in23(1'b0), .in24(1'b0), .in25(1'b0), .in26(1'b0), .in27(1'b0), .in28(1'b0), .in29(1'b0), .in30(1'b0),
    .in31(1'b0), .out(Q), .en_in(1'b1));  // open: gs, en_out
endmodule

module IRQ (
  input  done,
  input  Req,
  input  [2:0] State,
  input  Clock,
  input  Reset,
  input  ACK,
  output out_7
);

  wire and_1_out, and_2_out, or_1_out, s_r_ff_1_q;

  S_R_Flip_Flop s_r_ff_1 (.S(1'b1), .R(1'b0), .clk(Req), .Q(s_r_ff_1_q), .reset(or_1_out), .preset(1'b0));  // open: Qn
  or or_1 (or_1_out, Reset, ACK);
  and and_1 (and_1_out, s_r_ff_1_q, State[0], State[1], State[2]);
  and and_2 (and_2_out, s_r_ff_1_q, done);
  S_R_Flip_Flop s_r_ff_2 (
    .S(and_1_out), .R(ACK), .clk(Clock), .Q(out_7), .reset(Reset), .preset(and_2_out));  // open: Qn
endmodule

module ClockDivider (
  input  Clock,
  input  Reset,
  output C0,
  output C1,
  output C2,
  output C3
);

  wire buffer_1_out, buffer_2_out, buffer_3_out, buffer_4_out;
  wire [1:0] t_ff_1_q;

  buf buffer_1 (buffer_1_out, Clock);
  buf buffer_2 (buffer_2_out, buffer_1_out);
  buf buffer_3 (buffer_3_out, buffer_2_out);
  buf buffer_4 (buffer_4_out, buffer_3_out);
  buf buffer_5 (t_ff_1_q[1], buffer_4_out);
  T_Flip_Flop t_ff_1 (.T(1'b1), .clk(Clock), .Q(t_ff_1_q[0]), .reset(Reset), .preset(1'b0));  // open: Qn
  Decoder #(.enable("false"), .select(2)) decoder_1 (.out0(C0), .out1(C2), .out2(C3), .out3(C1), .sel(t_ff_1_q));

  // Notes on the sheet:
  //   Delay Matching
endmodule

module Nor24 (
  input  [23:0] in_1,
  output out_2
);

  nor nor_1 (out_2, in_1[0], in_1[1], in_1[2], in_1[3], in_1[4], in_1[5], in_1[6], in_1[7], in_1[8], in_1[9], in_1[10], in_1[11], in_1[12], in_1[13], in_1[14], in_1[15], in_1[16], in_1[17], in_1[18], in_1[19], in_1[20], in_1[21], in_1[22], in_1[23]);
endmodule
